# Fritzing sketch gps_ada_at328 (saved by Fritzing 0.8.7b)
circuit board: 9.3906cm x 6.76786cm

parts:
  U1 = atmega328 [package=dip]
  R1 = Resistor [tolerance=±5% resistance=4.7k package=THT]
  C1 = Ceramic Capacitor [capacitance=100nF package="100 mil [THT, multilayer]"]
  C2 = Electrolytic Capacitor [capacitance=10µF package="100 mil [THT, electrolytic]"]
  XTAL1 = Crystal [frequency="16 Mhz" package=THT]
  C3 = Capacitor [package=cap-pth-small2]
  C4 = Capacitor [package=cap-pth-small2]
  JP1 = Header 3 [package=molex-1x3_lock]
  JP2 = Header 3 [package=molex-1x3_lock]
  JP3 = Header 2 [package=molex-1x2_lock]
  JP4 = M16 [package=1x16_machine-pin-header_lock.004]
  Q1 = 2N7000 FET N-Channel [part_number=2N7000 package=TO92]
  R2 = Trimmer Potentiometer [maximum_resistance=10kΩ package=THT]
  R3 = Trimmer Potentiometer [maximum_resistance=10kΩ package=THT]
  JP5 = Header 2 [package=molex-1x2_lock]
  JP6 = Header 6 [package=molex-1x6_lock]
  R4 = Resistor [tolerance=±5% resistance=150 package=THT]

nets:
  N1: U1.RESET, R1.Pin_1, C1.0
  N2: U1.D0_(RX), JP1.2
  N3: U1.D1_(TX), JP1.3
  N4: U1.D2, Q1.gate
  5V: U1.VCC, U1.AVCC, R1.Pin_0, C2.+, JP3.1, JP4.2, JP4.15, R3.leg1
  GND: U1.GND, C2.-, C3.2, C4.2, JP3.2, JP4.5, Q1.source, R3.leg2, JP5.1
  N5: U1.XLAT1, XTAL1.pin_1, C3.1
  N6: U1.XLAT2, XTAL1.pin_0, C4.1
  N7: U1.D5_(PWM), JP6.1
  N8: U1.D6_(PWM), JP2.1
  N9: U1.D7, JP2.2
  N10: U1.D8, JP2.3
  N11: U1.D9_(PWM), JP6.2
  N12: U1.D10_(PWM), JP6.3
  N13: U1.D11_(PWM), JP6.4
  N14: U1.D12, JP6.5
  N15: U1.D13, JP6.6
  N16: U1.A0, JP4.14
  N17: U1.A1, JP4.13
  N18: U1.A2, JP4.12
  N19: U1.A3, JP4.11
  N20: U1.A4, JP4.6
  N21: U1.A5, JP4.4
  N22: C1.1, JP1.1
  N23: JP4.1, Q1.drain
  N24: JP4.3, R3.wiper
  N25: JP4.16, R4.Pin_1
  N26: R2.leg1, R4.Pin_0
  N27: R2.wiper, JP5.2

custom parts:
  2N7000 FET N-Channel: A 2N7000 MOSFET N-Channel Transistor
